// Logisim project chall.circ as structural Verilog: 1 circuit, main circuit main
module main (
  input  in_1
);

  wire xor_19_out;
  wire [7:0] multiplexer_1_out, multiplexer_9_out, multiplexer_17_out, multiplexer_25_out,
       multiplexer_33_out, multiplexer_41_out, multiplexer_49_out, multiplexer_57_out, multiplexer_65_out,
       multiplexer_73_out, multiplexer_81_out, multiplexer_89_out, multiplexer_97_out, multiplexer_105_out,
       multiplexer_113_out, multiplexer_121_out, multiplexer_129_out, not_1_out, not_2_out, not_3_out,
       undriven, undriven_2, undriven_3, undriven_4, undriven_5, undriven_6, undriven_7, undriven_8,
       undriven_9, undriven_10, undriven_11, undriven_12, undriven_13, undriven_14, undriven_15, undriven_16,
       undriven_17, undriven_18, undriven_19, undriven_20, undriven_21, undriven_22, undriven_23,
       undriven_24, undriven_25, undriven_26, undriven_27, undriven_28, undriven_29, undriven_30,
       undriven_31, undriven_32, undriven_33, undriven_34, undriven_35, undriven_36, undriven_37,
       undriven_38, undriven_39, undriven_40, undriven_41, undriven_42, undriven_43, undriven_44,
       undriven_45, undriven_46, undriven_47, undriven_48, undriven_49, undriven_50, undriven_51, xor_1_out,
       xor_2_out, xor_3_out, xor_4_out, xor_5_out, xor_6_out, xor_7_out, xor_8_out, xor_9_out, xor_10_out,
       xor_11_out, xor_12_out, xor_13_out, xor_14_out, xor_15_out, xor_16_out, xor_17_out, xor_20_out,
       xor_21_out, xor_22_out, xor_23_out, xor_24_out, xor_25_out, xor_26_out, xor_27_out, xor_28_out,
       xor_29_out, xor_30_out, xor_31_out, xor_32_out, xor_33_out, xor_34_out, xor_35_out, xor_36_out;

  assign xor_1_out = undriven ^ undriven_2;  // XOR_Gate xor_1, 8 bits wide
  assign xor_2_out = undriven_3 ^ undriven_4;  // XOR_Gate xor_2, 8 bits wide
  assign xor_3_out = undriven_5 ^ undriven_6;  // XOR_Gate xor_3, 8 bits wide
  assign xor_4_out = undriven_7 ^ undriven_8;  // XOR_Gate xor_4, 8 bits wide
  assign xor_5_out = undriven_9 ^ undriven_10;  // XOR_Gate xor_5, 8 bits wide
  assign xor_6_out = undriven_11 ^ undriven_12;  // XOR_Gate xor_6, 8 bits wide
  assign xor_7_out = undriven_13 ^ undriven_14;  // XOR_Gate xor_7, 8 bits wide
  assign xor_8_out = undriven_15 ^ undriven_16;  // XOR_Gate xor_8, 8 bits wide
  assign xor_9_out = undriven_17 ^ undriven_18;  // XOR_Gate xor_9, 8 bits wide
  assign xor_10_out = undriven_19 ^ undriven_20;  // XOR_Gate xor_10, 8 bits wide
  assign xor_11_out = undriven_21 ^ undriven_22;  // XOR_Gate xor_11, 8 bits wide
  assign xor_12_out = undriven_23 ^ undriven_24;  // XOR_Gate xor_12, 8 bits wide
  assign xor_13_out = undriven_25 ^ undriven_26;  // XOR_Gate xor_13, 8 bits wide
  assign xor_14_out = undriven_27 ^ undriven_28;  // XOR_Gate xor_14, 8 bits wide
  assign xor_15_out = undriven_29 ^ undriven_30;  // XOR_Gate xor_15, 8 bits wide
  assign xor_16_out = undriven_31 ^ undriven_32;  // XOR_Gate xor_16, 8 bits wide
  assign xor_17_out = undriven_33 ^ undriven_34;  // XOR_Gate xor_17, 8 bits wide
  Multiplexer multiplexer_1 (.in0(xor_9_out[0]), .out(multiplexer_1_out[0]), .sel(in_1));  // open: in1
  Multiplexer multiplexer_2 (.in0(xor_9_out[0]), .in1(xor_9_out[1]), .out(multiplexer_1_out[1]), .sel(in_1));
  Multiplexer multiplexer_3 (.in0(xor_9_out[1]), .in1(xor_9_out[2]), .out(multiplexer_1_out[2]), .sel(in_1));
  Multiplexer multiplexer_4 (.in0(xor_9_out[2]), .in1(xor_9_out[3]), .out(multiplexer_1_out[3]), .sel(in_1));
  Multiplexer multiplexer_5 (.in0(xor_9_out[3]), .in1(xor_9_out[4]), .out(multiplexer_1_out[4]), .sel(in_1));
  Multiplexer multiplexer_6 (.in0(xor_9_out[4]), .in1(xor_9_out[5]), .sel(in_1));  // open: out
  Multiplexer multiplexer_7 (.in0(xor_9_out[5]), .in1(xor_9_out[6]), .sel(in_1));  // open: out
  Multiplexer multiplexer_8 (.in0(xor_9_out[6]), .in1(xor_9_out[7]), .sel(in_1));  // open: out
  Multiplexer multiplexer_9 (.in0(xor_9_out[7]), .in1(xor_10_out[0]), .out(multiplexer_9_out[0]), .sel(in_1));
  Multiplexer multiplexer_10 (.in0(xor_10_out[0]), .in1(xor_10_out[1]), .out(multiplexer_9_out[1]), .sel(in_1));
  Multiplexer multiplexer_11 (.in0(xor_10_out[1]), .in1(xor_10_out[2]), .out(multiplexer_9_out[2]), .sel(in_1));
  Multiplexer multiplexer_12 (.in0(xor_10_out[2]), .in1(xor_10_out[3]), .out(multiplexer_9_out[3]), .sel(in_1));
  Multiplexer multiplexer_13 (.in0(xor_10_out[3]), .in1(xor_10_out[4]), .out(multiplexer_9_out[4]), .sel(in_1));
  Multiplexer multiplexer_14 (.in0(xor_10_out[4]), .in1(xor_10_out[5]), .out(multiplexer_9_out[5]), .sel(in_1));
  Multiplexer multiplexer_15 (.in0(xor_10_out[5]), .in1(xor_10_out[6]), .out(multiplexer_9_out[6]), .sel(in_1));
  Multiplexer multiplexer_16 (.in0(xor_10_out[6]), .in1(xor_10_out[7]), .out(multiplexer_9_out[7]), .sel(in_1));
  Multiplexer multiplexer_17 (.in0(xor_10_out[7]), .in1(xor_11_out[0]), .out(multiplexer_17_out[0]), .sel(in_1));
  Multiplexer multiplexer_18 (.in0(xor_11_out[0]), .in1(xor_11_out[1]), .out(multiplexer_17_out[1]), .sel(in_1));
  Multiplexer multiplexer_19 (.in0(xor_11_out[1]), .in1(xor_11_out[2]), .out(multiplexer_17_out[2]), .sel(in_1));
  Multiplexer multiplexer_20 (.in0(xor_11_out[2]), .in1(xor_11_out[3]), .out(multiplexer_17_out[3]), .sel(in_1));
  Multiplexer multiplexer_21 (.in0(xor_11_out[3]), .in1(xor_11_out[4]), .out(multiplexer_17_out[4]), .sel(in_1));
  Multiplexer multiplexer_22 (.in0(xor_11_out[4]), .in1(xor_11_out[5]), .out(multiplexer_17_out[5]), .sel(in_1));
  Multiplexer multiplexer_23 (.in0(xor_11_out[5]), .in1(xor_11_out[6]), .out(multiplexer_17_out[6]), .sel(in_1));
  Multiplexer multiplexer_24 (.in0(xor_11_out[6]), .in1(xor_11_out[7]), .out(multiplexer_17_out[7]), .sel(in_1));
  Multiplexer multiplexer_25 (.in0(xor_11_out[7]), .in1(xor_12_out[0]), .out(multiplexer_25_out[0]), .sel(in_1));
  Multiplexer multiplexer_26 (.in0(xor_12_out[0]), .in1(xor_12_out[1]), .out(multiplexer_25_out[1]), .sel(in_1));
  Multiplexer multiplexer_27 (.in0(xor_12_out[1]), .in1(xor_12_out[2]), .out(multiplexer_25_out[2]), .sel(in_1));
  Multiplexer multiplexer_28 (.in0(xor_12_out[2]), .in1(xor_12_out[3]), .out(multiplexer_25_out[3]), .sel(in_1));
  Multiplexer multiplexer_29 (.in0(xor_12_out[3]), .in1(xor_12_out[4]), .out(multiplexer_25_out[4]), .sel(in_1));
  Multiplexer multiplexer_30 (.in0(xor_12_out[4]), .in1(xor_12_out[5]), .out(multiplexer_25_out[5]), .sel(in_1));
  Multiplexer multiplexer_31 (.in0(xor_12_out[5]), .in1(xor_12_out[6]), .out(multiplexer_25_out[6]), .sel(in_1));
  Multiplexer multiplexer_32 (.in0(xor_12_out[6]), .in1(xor_12_out[7]), .out(multiplexer_25_out[7]), .sel(in_1));
  Multiplexer multiplexer_33 (.in0(xor_12_out[7]), .in1(xor_13_out[0]), .out(multiplexer_33_out[0]), .sel(in_1));
  Multiplexer multiplexer_34 (.in0(xor_13_out[0]), .in1(xor_13_out[1]), .out(multiplexer_33_out[1]), .sel(in_1));
  Multiplexer multiplexer_35 (.in0(xor_13_out[1]), .in1(xor_13_out[2]), .out(multiplexer_33_out[2]), .sel(in_1));
  Multiplexer multiplexer_36 (.in0(xor_13_out[2]), .in1(xor_13_out[3]), .out(multiplexer_33_out[3]), .sel(in_1));
  Multiplexer multiplexer_37 (.in0(xor_13_out[3]), .in1(xor_13_out[4]), .out(multiplexer_33_out[4]), .sel(in_1));
  Multiplexer multiplexer_38 (.in0(xor_13_out[4]), .in1(xor_13_out[5]), .out(multiplexer_33_out[5]), .sel(in_1));
  Multiplexer multiplexer_39 (.in0(xor_13_out[5]), .in1(xor_13_out[6]), .out(multiplexer_33_out[6]), .sel(in_1));
  Multiplexer multiplexer_40 (.in0(xor_13_out[6]), .in1(xor_13_out[7]), .out(multiplexer_33_out[7]), .sel(in_1));
  Multiplexer multiplexer_41 (.in0(xor_13_out[7]), .in1(xor_14_out[0]), .out(multiplexer_41_out[0]), .sel(in_1));
  Multiplexer multiplexer_42 (.in0(xor_14_out[0]), .in1(xor_14_out[1]), .out(multiplexer_41_out[1]), .sel(in_1));
  Multiplexer multiplexer_43 (.in0(xor_14_out[1]), .in1(xor_14_out[2]), .out(multiplexer_41_out[2]), .sel(in_1));
  Multiplexer multiplexer_44 (.in0(xor_14_out[2]), .in1(xor_14_out[3]), .out(multiplexer_41_out[3]), .sel(in_1));
  Multiplexer multiplexer_45 (.in0(xor_14_out[3]), .in1(xor_14_out[4]), .out(multiplexer_41_out[4]), .sel(in_1));
  Multiplexer multiplexer_46 (.in0(xor_14_out[4]), .in1(xor_14_out[5]), .out(multiplexer_41_out[5]), .sel(in_1));
  Multiplexer multiplexer_47 (.in0(xor_14_out[5]), .in1(xor_14_out[6]), .out(multiplexer_41_out[6]), .sel(in_1));
  Multiplexer multiplexer_48 (.in0(xor_14_out[6]), .in1(xor_14_out[7]), .out(multiplexer_41_out[7]), .sel(in_1));
  Multiplexer multiplexer_49 (.in0(xor_14_out[7]), .in1(xor_15_out[0]), .out(multiplexer_49_out[0]), .sel(in_1));
  Multiplexer multiplexer_50 (.in0(xor_15_out[0]), .in1(xor_15_out[1]), .out(multiplexer_49_out[1]), .sel(in_1));
  Multiplexer multiplexer_51 (.in0(xor_15_out[1]), .in1(xor_15_out[2]), .out(multiplexer_49_out[2]), .sel(in_1));
  Multiplexer multiplexer_52 (.in0(xor_15_out[2]), .in1(xor_15_out[3]), .out(multiplexer_49_out[3]), .sel(in_1));
  Multiplexer multiplexer_53 (.in0(xor_15_out[3]), .in1(xor_15_out[4]), .out(multiplexer_49_out[4]), .sel(in_1));
  Multiplexer multiplexer_54 (.in0(xor_15_out[4]), .in1(xor_15_out[5]), .out(multiplexer_49_out[5]), .sel(in_1));
  Multiplexer multiplexer_55 (.in0(xor_15_out[5]), .in1(xor_15_out[6]), .out(multiplexer_49_out[6]), .sel(in_1));
  Multiplexer multiplexer_56 (.in0(xor_15_out[6]), .in1(xor_15_out[7]), .out(multiplexer_49_out[7]), .sel(in_1));
  Multiplexer multiplexer_57 (.in0(xor_15_out[7]), .in1(xor_16_out[0]), .out(multiplexer_57_out[0]), .sel(in_1));
  Multiplexer multiplexer_58 (.in0(xor_16_out[0]), .in1(xor_16_out[1]), .out(multiplexer_57_out[1]), .sel(in_1));
  Multiplexer multiplexer_59 (.in0(xor_16_out[1]), .in1(xor_16_out[2]), .out(multiplexer_57_out[2]), .sel(in_1));
  Multiplexer multiplexer_60 (.in0(xor_16_out[2]), .in1(xor_16_out[3]), .out(multiplexer_57_out[3]), .sel(in_1));
  Multiplexer multiplexer_61 (.in0(xor_16_out[3]), .in1(xor_16_out[4]), .out(multiplexer_57_out[4]), .sel(in_1));
  Multiplexer multiplexer_62 (.in0(xor_16_out[4]), .in1(xor_16_out[5]), .out(multiplexer_57_out[5]), .sel(in_1));
  Multiplexer multiplexer_63 (.in0(xor_16_out[5]), .in1(xor_16_out[6]), .out(multiplexer_57_out[6]), .sel(in_1));
  Multiplexer multiplexer_64 (.in0(xor_16_out[6]), .in1(xor_16_out[7]), .out(multiplexer_57_out[7]), .sel(in_1));
  Multiplexer multiplexer_65 (.in0(xor_16_out[7]), .in1(xor_17_out[0]), .out(multiplexer_65_out[0]), .sel(in_1));
  Multiplexer multiplexer_66 (.in0(xor_17_out[0]), .in1(xor_17_out[1]), .out(multiplexer_65_out[1]), .sel(in_1));
  Multiplexer multiplexer_67 (.in0(xor_17_out[1]), .in1(xor_17_out[2]), .out(multiplexer_65_out[2]), .sel(in_1));
  Multiplexer multiplexer_68 (.in0(xor_17_out[2]), .in1(xor_17_out[3]), .out(multiplexer_65_out[3]), .sel(in_1));
  Multiplexer multiplexer_69 (.in0(xor_17_out[3]), .in1(xor_17_out[4]), .out(multiplexer_65_out[4]), .sel(in_1));
  Multiplexer multiplexer_70 (.in0(xor_17_out[4]), .in1(xor_17_out[5]), .out(multiplexer_65_out[5]), .sel(in_1));
  Multiplexer multiplexer_71 (.in0(xor_17_out[5]), .in1(xor_17_out[6]), .out(multiplexer_65_out[6]), .sel(in_1));
  Multiplexer multiplexer_72 (.in0(xor_17_out[6]), .in1(xor_17_out[7]), .out(multiplexer_65_out[7]), .sel(in_1));
  Multiplexer multiplexer_73 (.in0(xor_17_out[7]), .in1(xor_1_out[0]), .out(multiplexer_73_out[0]), .sel(in_1));
  Multiplexer multiplexer_74 (.in0(xor_1_out[0]), .in1(xor_1_out[1]), .out(multiplexer_73_out[1]), .sel(in_1));
  Multiplexer multiplexer_75 (.in0(xor_1_out[1]), .in1(xor_1_out[2]), .out(multiplexer_73_out[2]), .sel(in_1));
  Multiplexer multiplexer_76 (.in0(xor_1_out[2]), .in1(xor_1_out[3]), .out(multiplexer_73_out[3]), .sel(in_1));
  Multiplexer multiplexer_77 (.in0(xor_1_out[3]), .in1(xor_1_out[4]), .out(multiplexer_73_out[4]), .sel(in_1));
  Multiplexer multiplexer_78 (.in0(xor_1_out[4]), .in1(xor_1_out[5]), .out(multiplexer_73_out[5]), .sel(in_1));
  Multiplexer multiplexer_79 (.in0(xor_1_out[5]), .in1(xor_1_out[6]), .out(multiplexer_73_out[6]), .sel(in_1));
  Multiplexer multiplexer_80 (.in0(xor_1_out[6]), .in1(xor_1_out[7]), .out(multiplexer_73_out[7]), .sel(in_1));
  Multiplexer multiplexer_81 (.in0(xor_1_out[7]), .in1(xor_2_out[0]), .out(multiplexer_81_out[0]), .sel(in_1));
  Multiplexer multiplexer_82 (.in0(xor_2_out[0]), .in1(xor_2_out[1]), .out(multiplexer_81_out[1]), .sel(in_1));
  Multiplexer multiplexer_83 (.in0(xor_2_out[1]), .in1(xor_2_out[2]), .out(multiplexer_81_out[2]), .sel(in_1));
  Multiplexer multiplexer_84 (.in0(xor_2_out[2]), .in1(xor_2_out[3]), .out(multiplexer_81_out[3]), .sel(in_1));
  Multiplexer multiplexer_85 (.in0(xor_2_out[3]), .in1(xor_2_out[4]), .out(multiplexer_81_out[4]), .sel(in_1));
  Multiplexer multiplexer_86 (.in0(xor_2_out[4]), .in1(xor_2_out[5]), .out(multiplexer_81_out[5]), .sel(in_1));
  Multiplexer multiplexer_87 (.in0(xor_2_out[5]), .in1(xor_2_out[6]), .out(multiplexer_81_out[6]), .sel(in_1));
  Multiplexer multiplexer_88 (.in0(xor_2_out[6]), .in1(xor_2_out[7]), .out(multiplexer_81_out[7]), .sel(in_1));
  Multiplexer multiplexer_89 (.in0(xor_2_out[7]), .in1(xor_3_out[0]), .out(multiplexer_89_out[0]), .sel(in_1));
  Multiplexer multiplexer_90 (.in0(xor_3_out[0]), .in1(xor_3_out[1]), .out(multiplexer_89_out[1]), .sel(in_1));
  Multiplexer multiplexer_91 (.in0(xor_3_out[1]), .in1(xor_3_out[2]), .out(multiplexer_89_out[2]), .sel(in_1));
  Multiplexer multiplexer_92 (.in0(xor_3_out[2]), .in1(xor_3_out[3]), .out(multiplexer_89_out[3]), .sel(in_1));
  Multiplexer multiplexer_93 (.in0(xor_3_out[3]), .in1(xor_3_out[4]), .out(multiplexer_89_out[4]), .sel(in_1));
  Multiplexer multiplexer_94 (.in0(xor_3_out[4]), .in1(xor_3_out[5]), .out(multiplexer_89_out[5]), .sel(in_1));
  Multiplexer multiplexer_95 (.in0(xor_3_out[5]), .in1(xor_3_out[6]), .out(multiplexer_89_out[6]), .sel(in_1));
  Multiplexer multiplexer_96 (.in0(xor_3_out[6]), .in1(xor_3_out[7]), .out(multiplexer_89_out[7]), .sel(in_1));
  Multiplexer multiplexer_97 (.in0(xor_3_out[7]), .in1(xor_4_out[0]), .out(multiplexer_97_out[0]), .sel(in_1));
  Multiplexer multiplexer_98 (.in0(xor_4_out[0]), .in1(xor_4_out[1]), .out(multiplexer_97_out[1]), .sel(in_1));
  Multiplexer multiplexer_99 (.in0(xor_4_out[1]), .in1(xor_4_out[2]), .out(multiplexer_97_out[2]), .sel(in_1));
  Multiplexer multiplexer_100 (.in0(xor_4_out[2]), .in1(xor_4_out[3]), .out(multiplexer_97_out[3]), .sel(in_1));
  Multiplexer multiplexer_101 (.in0(xor_4_out[3]), .in1(xor_4_out[4]), .out(multiplexer_97_out[4]), .sel(in_1));
  Multiplexer multiplexer_102 (.in0(xor_4_out[4]), .in1(xor_4_out[5]), .out(multiplexer_97_out[5]), .sel(in_1));
  Multiplexer multiplexer_103 (.in0(xor_4_out[5]), .in1(xor_4_out[6]), .out(multiplexer_97_out[6]), .sel(in_1));
  Multiplexer multiplexer_104 (.in0(xor_4_out[6]), .in1(xor_4_out[7]), .out(multiplexer_97_out[7]), .sel(in_1));
  Multiplexer multiplexer_105 (.in0(xor_4_out[7]), .in1(xor_5_out[0]), .out(multiplexer_105_out[0]), .sel(in_1));
  Multiplexer multiplexer_106 (.in0(xor_5_out[0]), .in1(xor_5_out[1]), .out(multiplexer_105_out[1]), .sel(in_1));
  Multiplexer multiplexer_107 (.in0(xor_5_out[1]), .in1(xor_5_out[2]), .out(multiplexer_105_out[2]), .sel(in_1));
  Multiplexer multiplexer_108 (.in0(xor_5_out[2]), .in1(xor_5_out[3]), .out(multiplexer_105_out[3]), .sel(in_1));
  Multiplexer multiplexer_109 (.in0(xor_5_out[3]), .in1(xor_5_out[4]), .out(multiplexer_105_out[4]), .sel(in_1));
  Multiplexer multiplexer_110 (.in0(xor_5_out[4]), .in1(xor_5_out[5]), .out(multiplexer_105_out[5]), .sel(in_1));
  Multiplexer multiplexer_111 (.in0(xor_5_out[5]), .in1(xor_5_out[6]), .out(multiplexer_105_out[6]), .sel(in_1));
  Multiplexer multiplexer_112 (.in0(xor_5_out[6]), .in1(xor_5_out[7]), .out(multiplexer_105_out[7]), .sel(in_1));
  Multiplexer multiplexer_113 (.in0(xor_5_out[7]), .in1(xor_6_out[0]), .out(multiplexer_113_out[0]), .sel(in_1));
  Multiplexer multiplexer_114 (.in0(xor_6_out[0]), .in1(xor_6_out[1]), .out(multiplexer_113_out[1]), .sel(in_1));
  Multiplexer multiplexer_115 (.in0(xor_6_out[1]), .in1(xor_6_out[2]), .out(multiplexer_113_out[2]), .sel(in_1));
  Multiplexer multiplexer_116 (.in0(xor_6_out[2]), .in1(xor_6_out[3]), .out(multiplexer_113_out[3]), .sel(in_1));
  Multiplexer multiplexer_117 (.in0(xor_6_out[3]), .in1(xor_6_out[4]), .out(multiplexer_113_out[4]), .sel(in_1));
  Multiplexer multiplexer_118 (.in0(xor_6_out[4]), .in1(xor_6_out[5]), .out(multiplexer_113_out[5]), .sel(in_1));
  Multiplexer multiplexer_119 (.in0(xor_6_out[5]), .in1(xor_6_out[6]), .out(multiplexer_113_out[6]), .sel(in_1));
  Multiplexer multiplexer_120 (.in0(xor_6_out[6]), .in1(xor_6_out[7]), .out(multiplexer_113_out[7]), .sel(in_1));
  Multiplexer multiplexer_121 (.in0(xor_6_out[7]), .in1(xor_7_out[0]), .out(multiplexer_121_out[0]), .sel(in_1));
  Multiplexer multiplexer_122 (.in0(xor_7_out[0]), .in1(xor_7_out[1]), .out(multiplexer_121_out[1]), .sel(in_1));
  Multiplexer multiplexer_123 (.in0(xor_7_out[1]), .in1(xor_7_out[2]), .out(multiplexer_121_out[2]), .sel(in_1));
  Multiplexer multiplexer_124 (.in0(xor_7_out[2]), .in1(xor_7_out[3]), .out(multiplexer_121_out[3]), .sel(in_1));
  Multiplexer multiplexer_125 (.in0(xor_7_out[3]), .in1(xor_7_out[4]), .out(multiplexer_121_out[4]), .sel(in_1));
  Multiplexer multiplexer_126 (.in0(xor_7_out[4]), .in1(xor_7_out[5]), .out(multiplexer_121_out[5]), .sel(in_1));
  Multiplexer multiplexer_127 (.in0(xor_7_out[5]), .in1(xor_7_out[6]), .out(multiplexer_121_out[6]), .sel(in_1));
  Multiplexer multiplexer_128 (.in0(xor_7_out[6]), .in1(xor_7_out[7]), .out(multiplexer_121_out[7]), .sel(in_1));
  Multiplexer multiplexer_129 (.in0(xor_7_out[7]), .in1(xor_8_out[0]), .out(multiplexer_129_out[0]), .sel(in_1));
  Multiplexer multiplexer_130 (.in0(xor_8_out[0]), .in1(xor_8_out[1]), .out(multiplexer_129_out[1]), .sel(in_1));
  Multiplexer multiplexer_131 (.in0(xor_8_out[1]), .in1(xor_8_out[2]), .out(multiplexer_129_out[2]), .sel(in_1));
  Multiplexer multiplexer_132 (.in0(xor_8_out[2]), .in1(xor_8_out[3]), .out(multiplexer_129_out[3]), .sel(in_1));
  Multiplexer multiplexer_133 (.in0(xor_8_out[3]), .in1(xor_8_out[4]), .out(multiplexer_129_out[4]), .sel(in_1));
  Multiplexer multiplexer_134 (.in0(xor_8_out[4]), .in1(xor_8_out[5]), .out(multiplexer_129_out[5]), .sel(in_1));
  Multiplexer multiplexer_135 (.in0(xor_8_out[5]), .in1(xor_8_out[6]), .out(multiplexer_129_out[6]), .sel(in_1));
  Multiplexer multiplexer_136 (.in0(xor_8_out[6]), .in1(xor_8_out[7]), .out(multiplexer_129_out[7]), .sel(in_1));
  xor xor_18 (multiplexer_1_out[7], multiplexer_1_out[0], multiplexer_1_out[1]);
  xor xor_19 (xor_19_out, multiplexer_1_out[2], multiplexer_1_out[3]);
  and and_1 (multiplexer_1_out[6], xor_19_out, multiplexer_1_out[4]);
  or or_1 (multiplexer_1_out[5], xor_19_out, multiplexer_1_out[4]);
  assign xor_20_out = undriven_35 ^ multiplexer_1_out;  // XOR_Gate xor_20, 8 bits wide
  assign xor_21_out = undriven_36 ^ multiplexer_9_out;  // XOR_Gate xor_21, 8 bits wide
  assign xor_22_out = undriven_37 ^ multiplexer_17_out;  // XOR_Gate xor_22, 8 bits wide
  assign xor_23_out = undriven_38 ^ multiplexer_25_out;  // XOR_Gate xor_23, 8 bits wide
  assign xor_24_out = undriven_39 ^ multiplexer_33_out;  // XOR_Gate xor_24, 8 bits wide
  assign xor_25_out = undriven_40 ^ multiplexer_41_out;  // XOR_Gate xor_25, 8 bits wide
  assign xor_26_out = undriven_41 ^ multiplexer_49_out;  // XOR_Gate xor_26, 8 bits wide
  assign xor_27_out = undriven_42 ^ multiplexer_57_out;  // XOR_Gate xor_27, 8 bits wide
  assign xor_28_out = undriven_43 ^ multiplexer_65_out;  // XOR_Gate xor_28, 8 bits wide
  assign xor_29_out = undriven_44 ^ multiplexer_73_out;  // XOR_Gate xor_29, 8 bits wide
  assign xor_30_out = undriven_45 ^ multiplexer_81_out;  // XOR_Gate xor_30, 8 bits wide
  assign xor_31_out = undriven_46 ^ multiplexer_89_out;  // XOR_Gate xor_31, 8 bits wide
  assign xor_32_out = undriven_47 ^ multiplexer_97_out;  // XOR_Gate xor_32, 8 bits wide
  assign xor_33_out = undriven_48 ^ multiplexer_105_out;  // XOR_Gate xor_33, 8 bits wide
  assign xor_34_out = undriven_49 ^ multiplexer_113_out;  // XOR_Gate xor_34, 8 bits wide
  assign xor_35_out = undriven_50 ^ multiplexer_121_out;  // XOR_Gate xor_35, 8 bits wide
  assign xor_36_out = undriven_51 ^ multiplexer_129_out;  // XOR_Gate xor_36, 8 bits wide
  assign not_1_out = ~xor_32_out;  // NOT_Gate not_1, 8 bits wide
  assign not_2_out = ~xor_34_out;  // NOT_Gate not_2, 8 bits wide
  assign not_3_out = ~xor_36_out;  // NOT_Gate not_3, 8 bits wide

  // Notes on the sheet:
  //   00110111
  //   01111101
  //   00110111
  //   01111010
  //   00110111
  //   01011010
  //   00110111
  //   01111010
  //   00110111
  //   01011111
  //   00110111
  //   01100100
  //   00110111
  //   01100101
  //   00110111
  //   01110010 
  //   00110111
  //   00110111
  //   00110111
  //   01101001
  //   00110111
  //   01110100
  //   00110111
  //   01011111
  //   00110111
  //   01101001
  //   00110111
  //   01111011
  //   00110111
  //   01010111
  //   00110111
  //   01000011
  //   00110111
  //   01001110
  //   1
  //   0
  //   1
  //   0
  //   0
  //   1
  //   1000001
  //   00111001
  //   00111001
  //   00111001
  //   00111001
  //   00111001
  //   00111001
  //   00111001
  //   00111001
  //   00111001
  //   00111001
  //   00111001
  //   00111001
  //   00111001
  //   00111001
  //   00111001
  //   00111001
  //   00111001
  //   OUTPUT
endmodule
